# Fritzing sketch Electronic shema_concept (saved by Fritzing 0.9.3b)

parts:
  ESP8266_Breakout = Adafruit HUZZAH ESP8266 Breakout [part_number=2471]
  CAP1188 = MPR121 Breakout
  WS2812b = ws2812b [package="smd 2812b"]
  LM1084IT_ou_LF33CV = V_REG_LD1117VXX [package=78xxl]
  Li-ion_3Ah = LIPO-1000mAh [package=lipo-1000]
  Li-ion_USB_charger = V_REG_LD1117VXX [package=78xxl]
  USB = USB connector [package=THT]
  2_2-4_2V_to_5V_Step-Up = V_REG_LD1117VXX [package=78xxl]
  C1 = Electrolytic Capacitor [capacitance=47µF package="100 mil [THT, electrolytic]"]
  R1 = Resistor [tolerance=±5% resistance=220 package=THT]
  R2 = Resistor [tolerance=±5% resistance=220 package=THT]
  R3 = Resistor [tolerance=±5% resistance=2k package=THT]
  R4 = Resistor [tolerance=±5% resistance=2k package=THT]
  Touch = Header 8 [package=1x08_smd]
  WS2812b_3 = ws2812b [package="smd 2812b"]
  Wifi_MQTT_Rx_/_Tx = LEDs [package=led10mm]
  R5 = Resistor [tolerance=±5% resistance=470 package=THT]
  WS2812b_3_to_43 = ws2812b [package="smd 2812b"]
  SP1 = SPEAKER [package=pcb_mount_speaker]
  2N2222_1 = TRANSISTOR_NPN [package=to-92]
  2N2222_2 = TRANSISTOR_NPN [package=to-92]
  R6 = Resistor [tolerance=±5% resistance=47k package=THT]
  R7 = Resistor [tolerance=±5% resistance=2.7k package=THT]
  2N2222_3 = TRANSISTOR_NPN [package=to-92]
  2N2222_4 = TRANSISTOR_NPN [package=to-92]
  R8 = Resistor [tolerance=±5% resistance=47k package=THT]
  R9 = Resistor [tolerance=±5% resistance=2.7k package=THT]
  2N2222_5 = TRANSISTOR_NPN [package=to-92]
  R10 = Resistor [tolerance=±5% resistance=2.7k package=THT]
  2N2222_6 = TRANSISTOR_NPN [package=to-92]
  R11 = Resistor [tolerance=±5% resistance=47k package=THT]
  R12 = Resistor [tolerance=±5% resistance=2.7k package=THT]
  R13 = Resistor [tolerance=±5% resistance=2.7k package=THT]
  C2 = Electrolytic Capacitor [capacitance=470µF package="100 mil [THT, electrolytic]"]
  R14 = Resistor [tolerance=±5% resistance=47 package=THT]
  R15 = Resistor [tolerance=±5% resistance=47 package=THT]
  R16 = Resistor [tolerance=±5% resistance=47k package=THT]
  R17 = Resistor [tolerance=±5% resistance=47k package=THT]
  R18 = Resistor [tolerance=±5% resistance=4.7k package=THT]
  R19 = Resistor [tolerance=±5% resistance=4.7k package=THT]
  C3 = Electrolytic Capacitor [capacitance=10µF package="100 mil [THT, electrolytic]"]
  R20 = Resistor [tolerance=±5% resistance=47k package=THT]
  R21 = Resistor [tolerance=±5% resistance=47k package=THT]
  R22 = Resistor [tolerance=±5% resistance=47k package=THT]
  D1 = Schottky Diode [part_number=1N5818 package="300 mil [THT]"]
  7805 = Voltage Regulator [package=to220-igo]
  J1 = Power Jack [package=power_jack_combo]
  C4 = Electrolytic Capacitor [capacitance=10µF package="100 mil [THT, electrolytic]"]
  C5 = Electrolytic Capacitor [capacitance=10µF package="100 mil [THT, electrolytic]"]
  S5 = SWITCH-DPDT [package=eg2211]
  D4 = Schottky Diode [part_number=1N5818 package="300 mil [THT]"]
  D5 = Schottky Diode [part_number=1N5818 package="300 mil [THT]"]
  2N2907_1 = PNP-Transistor [package="TO92 [THT]"]
  2N2907_2 = PNP-Transistor [package="TO92 [THT]"]
  2N2907_3 = PNP-Transistor [package="TO92 [THT]"]

nets:
  GND: ESP8266_Breakout.GND, CAP1188.GND, WS2812b.VSS, LM1084IT_ou_LF33CV.GND, Li-ion_3Ah.-, Li-ion_USB_charger.GND, USB.chassis5, 2_2-4_2V_to_5V_Step-Up.GND, C1.-, WS2812b_3.VSS, Wifi_MQTT_Rx_/_Tx.A, WS2812b_3_to_43.VSS, 2N2222_2.E, R6.Pin_0, 2N2222_4.E, R8.Pin_0, 2N2222_5.E, 2N2222_6.E, R11.Pin_0, C3.-, R21.Pin_0, R22.Pin_0, 7805.GND, J1.PWR, C4.-, C5.-
  5V: ESP8266_Breakout.V+, WS2812b.VDD, LM1084IT_ou_LF33CV.IN, C1.+, WS2812b_3.VDD, WS2812b_3_to_43.VDD, R16.Pin_0, R17.Pin_0, D1.cathode, S5.1, 2N2907_2.E, 2N2907_3.E
  N1: ESP8266_Breakout.#13, R5.Pin_1
  N2: ESP8266_Breakout.#12, R12.Pin_0
  N3: ESP8266_Breakout.#16, R7.Pin_0, R13.Pin_0
  N4: ESP8266_Breakout.RX, WS2812b.DIN
  N5: ESP8266_Breakout.#5, R1.Pin_0, R4.Pin_0
  N6: ESP8266_Breakout.#4, R2.Pin_0, R3.Pin_0
  3.3V: ESP8266_Breakout.3V, CAP1188.3.3V, LM1084IT_ou_LF33CV.OUT, R3.Pin_1, R4.Pin_1, R10.Pin_0, C3.+, R20.Pin_1, 2N2907_1.E
  N7: CAP1188.SCL, R2.Pin_1
  N8: CAP1188.SDA, R1.Pin_1
  N9: CAP1188.ELE7, Touch.8
  N10: CAP1188.ELE6, Touch.7
  N11: CAP1188.ELE5, Touch.6
  N12: CAP1188.ELE4, Touch.5
  N13: CAP1188.ELE3, Touch.4
  N14: CAP1188.ELE2, Touch.3
  N15: CAP1188.ELE1, Touch.2
  N16: CAP1188.ELE0, Touch.1
  N17: WS2812b.DOUT, WS2812b_3.DIN
  N18: Li-ion_3Ah.+, Li-ion_USB_charger.OUT, S5.5
  N19: Li-ion_USB_charger.IN, S5.2, D4.cathode, D5.cathode
  N20: USB.5V, D4.anode
  N21: 2_2-4_2V_to_5V_Step-Up.OUT, D1.anode
  N22: 2_2-4_2V_to_5V_Step-Up.IN, S5.4
  N23: WS2812b_3.DOUT, WS2812b_3_to_43.DIN
  N24: Wifi_MQTT_Rx_/_Tx.C, R5.Pin_0
  N25: SP1.+, C2.-
  N26: SP1.-, 2N2222_4.C, R14.Pin_0
  N27: 2N2222_1.E, 2N2222_2.B, R6.Pin_1
  N28: 2N2222_1.B, R7.Pin_1, 2N2222_5.C, R22.Pin_1
  N29: 2N2222_1.C, R19.Pin_0
  N30: 2N2222_2.C, C2.+, R15.Pin_0
  N31: 2N2222_3.E, 2N2222_4.B, R8.Pin_1
  N32: 2N2222_3.B, R9.Pin_1, R21.Pin_1
  N33: 2N2222_3.C, R18.Pin_0
  N34: R9.Pin_0, 2N2907_1.C
  N35: 2N2222_5.B, R10.Pin_1, 2N2222_6.C
  N36: 2N2222_6.B, R11.Pin_1, R12.Pin_1
  N37: R13.Pin_1, R20.Pin_0, 2N2907_1.B
  N38: R14.Pin_1, 2N2907_2.C
  N39: R15.Pin_1, 2N2907_3.C
  N40: R16.Pin_1, R19.Pin_1, 2N2907_2.B
  N41: R17.Pin_1, R18.Pin_1, 2N2907_3.B
  N42: 7805.IN, J1.GND, C5.+
  N43: 7805.OUT, C4.+, D5.anode

notes:
  OPTIONAL
